# Fritzing sketch MIDI_Connections (saved by Fritzing 1.0.0rc)
stripboards: 1

parts:
  Hat1 = Pisound Micro [package=THT]
  U1 = MIDI_CONN_FEMALE [package=din_5_female]
  U2 = MIDI_CONN_FEMALE [package=din_5_female]
  LED1 = LEDs [package=led10mm]
  R1 = Resistor [tolerance=±5% power=0.25W resistance=1000 package=THT]
  LED2 = LEDs [package=led10mm]
  R2 = Resistor [tolerance=±5% power=0.25W resistance=1000 package=THT]

nets:
  N1: Hat1.A20, U2.NC1, LED1.C, LED2.C
  N2: Hat1.A21, U1.MIDI_IN
  N3: Hat1.A22, U2.MIDI_OUT
  N4: Hat1.A23, U1.MIDI_OUT
  N5: Hat1.A24, U2.MIDI_IN
  N6: Hat1.A27, R2.Pin_1
  N7: Hat1.A28, R1.Pin_1
  N8: LED1.A, R1.Pin_0
  N9: LED2.A, R2.Pin_0

notes:
  MIDI OUTPUT
  MIDI INPUT
  C -
  A +
